# Fritzing sketch SelfBalancingV4_Fritzing (saved by Fritzing 0.9.2b)
breadboards: 1

parts:
  EspruinoPico = Espruino Pico
  MPU6050-GY521 = MPU-6050 Board GY-521 [form="♀ (female)" package=THT]
  DRV_1 = DRV 8825 Stepper Motor Carrier, High Current [part_number="DRV 8825"]
  DRV_2 = DRV 8825 Stepper Motor Carrier, High Current [part_number="DRV 8825"]
  BiPolar_Stepper = Stepper Motor - Bipolar
  BiPolar_Stepper_2 = Stepper Motor - Bipolar
  C1 = Electrolytic Capacitor [capacitance=100µF package="200 mil [THT, electrolytic]"]
  VCC1 = Battery block 9V
  U1 = ESP8266 WiFi Module [part_number=ESP8266]
  3_3V = V_REG_LD1117VXX [package=78xxl]

nets:
  N1: EspruinoPico.Vin, DRV_1.VMOT, DRV_2.VMOT, C1.+, VCC1.+, 3_3V.IN
  N2: EspruinoPico.B10, DRV_1.ENABLE
  N3: EspruinoPico.B1, DRV_1.DIRECTION
  N4: EspruinoPico.A7, DRV_1.STEP
  N5: EspruinoPico.A3, U1.TXD
  N6: EspruinoPico.A2, U1.RXD
  N7: EspruinoPico.A8, MPU6050-GY521.pin8
  N8: EspruinoPico.B7, MPU6050-GY521.pin4
  N9: EspruinoPico.B6, MPU6050-GY521.pin3
  N10: EspruinoPico.B5, DRV_2.ENABLE
  N11: EspruinoPico.B4, DRV_2.STEP
  N12: EspruinoPico.B3, DRV_2.DIRECTION
  GND: EspruinoPico.GND, MPU6050-GY521.pin2, DRV_1.GND, DRV_1.GROUND, DRV_2.GND, DRV_2.GROUND, C1.-, VCC1.-, U1.GND, 3_3V.GND
  N13: MPU6050-GY521.pin1, MPU6050-GY521.pin7, DRV_1.RESET, DRV_1.SLEEP, DRV_2.RESET, DRV_2.SLEEP, U1.VCC, U1.CH_PD, 3_3V.OUT
  N14: DRV_1.OUT_2B, BiPolar_Stepper.D
  N15: DRV_1.OUT_2A, BiPolar_Stepper.B
  N16: DRV_1.OUT_1A, BiPolar_Stepper.C
  N17: DRV_1.OUT_1B, BiPolar_Stepper.A
  N18: DRV_2.OUT_2B, BiPolar_Stepper_2.D
  N19: DRV_2.OUT_2A, BiPolar_Stepper_2.B
  N20: DRV_2.OUT_1A, BiPolar_Stepper_2.C
  N21: DRV_2.OUT_1B, BiPolar_Stepper_2.A

custom parts:
  MPU-6050 Board GY-521: Acelerometro y Giroscopio MPU-6050 Board GY-521
  DRV 8825 Stepper Motor Carrier, High Current: This is a Stepper Motor Controller for integrated circuits. This breakout board for TI’s DRV8825 microstepping bipolar stepper motor driver features adjustable current limiting, over-current and over-temperature protection, and six microstep resolutions (down to 1/32-step). It operates from 8.2 V to 45 V and can deliver up to approximately 1.5 A per phase without a heat sink or forced air flow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
  ESP8266 WiFi Module: Generic WiFi Module based on the ESP8266 with onboard PCB antenna and UART communications
